// Digital circuit alu-32b-final.dig as structural Verilog
module alu_32b_final (
  input  [31:0] A,
  input  [31:0] B,
  input  [31:0] C,
  input  [4:0] alu_ctrl,
  input  [7:0] opcode,
  input  CLK,
  input  FLAG_WE,
  input  flagIsNotZ,
  output [31:0] OUT,
  output [14:0] CSR_FLAG
);

  wire _74377_1_pin1, aeff31, beff31, C_out, cin, cout0, cout1, cout2, cout3, cout4, cout5, cout6, GT_sign,
       GT_unsign, GTE_sign, LT_sign, LTE_sign, LTE_unsign, nand_1_out, nand_2_out, nand_3_out, nand_4_out,
       nC_out, nN_out, not_6_out, not_8_out, not_9_out, not_10_out, not_11_out, not_12_out, not_13_out,
       not_14_out, not_15_out, not_16_out, not_17_out, not_18_out, not_19_out, not_20_out, not_21_out,
       not_22_out, not_23_out, not_24_out, not_25_out, not_26_out, not_27_out, not_28_out, not_29_out,
       not_30_out, not_31_out, not_32_out, not_33_out, not_34_out, not_35_out, not_36_out, not_37_out,
       not_38_out, not_39_out, nV_out, nZ_out, or_4_out, or_5_out, q15, sum31, V_out, xor_1_out, xor_2_out,
       Z_out;

  Multiplexer #(.Selector_Bits(3)) multiplexer_1 (
    .sel(alu_ctrl[4:2]), .in_0(1'b0), .in_1(1'b1), .in_2(CSR_FLAG[4]), .in_3(CSR_FLAG[0]),
    .in_4(CSR_FLAG[2]), .in_5(CSR_FLAG[6]), .in_6(CSR_FLAG[5]), .in_7(CSR_FLAG[8]), .out(cin));
  // alu_4b_final alu_4b_final_1: pin names not known; wires that end beside it: A[3:0], B[3:0], opcode, C[3:0], alu_ctrl[1:0], cin, OUT[3:0], cout0
  // alu_4b_final alu_4b_final_2: pin names not known; wires that end beside it: A[19:16], B[19:16], opcode, C[19:16], alu_ctrl[1:0], cout3, OUT[19:16], cout4
  // alu_4b_final alu_4b_final_3: pin names not known; wires that end beside it: A[7:4], B[7:4], opcode, C[7:4], alu_ctrl[1:0], cout0, OUT[7:4], cout1
  // alu_4b_final alu_4b_final_4: pin names not known; wires that end beside it: A[23:20], B[23:20], opcode, C[23:20], alu_ctrl[1:0], cout4, OUT[23:20], cout5
  // alu_4b_final alu_4b_final_5: pin names not known; wires that end beside it: A[11:8], B[11:8], opcode, OUT[11:8], alu_ctrl[1:0], cout1, OUT[11:8], cout2
  // alu_4b_final alu_4b_final_6: pin names not known; wires that end beside it: A[27:24], B[27:24], opcode, C[27:24], alu_ctrl[1:0], cout5, OUT[27:24], cout6
  alu_4b_final alu_4b_final_7 (
    .A(A[15:12]), .B(B[15:12]), .OPCODE(opcode), .C(OUT[15:12]), .alu_ctrl(alu_ctrl[1:0]), .cin(cout2),
    .Out(OUT[15:12]), .cout(cout3));  // open: sum3, aeff3, beff3
  alu_4b_final alu_4b_final_8 (
    .A(A[31:28]), .B(B[31:28]), .OPCODE(opcode), .C(C[31:28]), .alu_ctrl(alu_ctrl[1:0]), .cin(cout6),
    .Out(OUT[31:28]), .cout(C_out), .sum3(sum31), .aeff3(aeff31), .beff3(beff31));
  not not_1 (Z_out, nZ_out);
  not not_2 (nC_out, C_out);
  not not_3 (nV_out, V_out);
  not not_4 (nN_out, OUT[31]);
  _74377 _74377_1 (
    .pin1(_74377_1_pin1), .pin2(CSR_FLAG[0]), .pin3(Z_out), .pin4(nZ_out), .pin5(CSR_FLAG[1]),
    .pin6(CSR_FLAG[2]), .pin7(OUT[31]), .pin8(nN_out), .pin9(CSR_FLAG[3]), .pin10(1'b0), .pin11(CLK),
    .pin12(CSR_FLAG[4]), .pin13(C_out), .pin14(nC_out), .pin15(CSR_FLAG[5]), .pin16(CSR_FLAG[6]),
    .pin17(V_out), .pin18(nV_out), .pin19(CSR_FLAG[7]), .pin20(1'b1));
  not not_5 (_74377_1_pin1, FLAG_WE);
  and and_1 (GT_unsign, nZ_out, C_out);
  or or_1 (LTE_unsign, nZ_out, nC_out);
  and and_2 (V_out, xor_2_out, xor_1_out);
  and and_3 (GT_sign, nZ_out, GTE_sign);
  or or_2 (LTE_sign, Z_out, LT_sign);
  not not_6 (not_6_out, FLAG_WE);
  not not_7 (GTE_sign, LT_sign);
  _74377 _74377_2 (
    .pin1(not_6_out), .pin2(CSR_FLAG[8]), .pin3(LT_sign), .pin4(LTE_sign), .pin5(CSR_FLAG[9]),
    .pin6(CSR_FLAG[10]), .pin7(GT_sign), .pin8(GTE_sign), .pin9(CSR_FLAG[11]), .pin10(1'b0), .pin11(CLK),
    .pin12(CSR_FLAG[14]), .pin13(GT_unsign), .pin14(LTE_unsign), .pin15(CSR_FLAG[13]), .pin17(1'b0),
    .pin18(1'b0), .pin19(q15), .pin20(1'b1));  // open: pin16
  xor xor_1 (xor_1_out, sum31, aeff31);
  xor xor_2 (xor_2_out, beff31, sum31);
  xor xor_3 (LT_sign, V_out, OUT[31]);
  or or_3 (nZ_out, or_5_out, or_4_out);
  or or_4 (or_4_out, nand_2_out, nand_1_out);
  or or_5 (or_5_out, nand_4_out, nand_3_out);
  nand nand_1 (nand_1_out, not_15_out, not_14_out, not_13_out, not_12_out, not_11_out, not_10_out, not_9_out, not_8_out);
  nand nand_2 (nand_2_out, not_23_out, not_22_out, not_21_out, not_20_out, not_19_out, not_18_out, not_17_out, not_16_out);
  nand nand_3 (nand_3_out, not_31_out, not_30_out, not_29_out, not_28_out, not_27_out, not_26_out, not_25_out, not_24_out);
  nand nand_4 (nand_4_out, not_39_out, not_38_out, not_37_out, not_36_out, not_35_out, not_34_out, not_33_out, not_32_out);
  not not_8 (not_8_out, OUT[0]);
  not not_9 (not_9_out, OUT[1]);
  not not_10 (not_10_out, OUT[2]);
  not not_11 (not_11_out, OUT[3]);
  not not_12 (not_12_out, OUT[4]);
  not not_13 (not_13_out, OUT[5]);
  not not_14 (not_14_out, OUT[6]);
  not not_15 (not_15_out, OUT[7]);
  not not_16 (not_16_out, OUT[8]);
  not not_17 (not_17_out, OUT[9]);
  not not_18 (not_18_out, OUT[10]);
  not not_19 (not_19_out, OUT[11]);
  not not_20 (not_20_out, OUT[12]);
  not not_21 (not_21_out, OUT[13]);
  not not_22 (not_22_out, OUT[14]);
  not not_23 (not_23_out, OUT[15]);
  not not_24 (not_24_out, OUT[16]);
  not not_25 (not_25_out, OUT[17]);
  not not_26 (not_26_out, OUT[18]);
  not not_27 (not_27_out, OUT[19]);
  not not_28 (not_28_out, OUT[20]);
  not not_29 (not_29_out, OUT[21]);
  not not_30 (not_30_out, OUT[22]);
  not not_31 (not_31_out, OUT[23]);
  not not_32 (not_32_out, OUT[24]);
  not not_33 (not_33_out, OUT[25]);
  not not_34 (not_34_out, OUT[26]);
  not not_35 (not_35_out, OUT[27]);
  not not_36 (not_36_out, OUT[28]);
  not not_37 (not_37_out, OUT[29]);
  not not_38 (not_38_out, OUT[30]);
  not not_39 (not_39_out, OUT[31]);

  assign CSR_FLAG[12] = flagIsNotZ;

  // Other names for the same wires on the sheet: a4[3:0] = A[3:0]; a8[3:0] = A[7:4]; a12[3:0] = A[11:8];
  //   a16[3:0] = A[15:12]; a20[3:0] = A[19:16]; a24[3:0] = A[23:20]; a28[3:0] = A[27:24]; a32[3:0] = A[31:28];
  //   alu_ctrl_in[1:0] = alu_ctrl[1:0]; cin_SEL[2:0] = alu_ctrl[4:2]; b4[3:0] = B[3:0]; b8[3:0] = B[7:4];
  //   b12[3:0] = B[11:8]; b16[3:0] = B[15:12]; b20[3:0] = B[19:16]; b24[3:0] = B[23:20]; b28[3:0] = B[27:24];
  //   b32[3:0] = B[31:28]; c4[3:0] = C[3:0]; c8[3:0] = C[7:4]; c12[3:0] = C[11:8]; c16[3:0] = C[15:12];
  //   c20[3:0] = C[19:16]; c24[3:0] = C[23:20]; c28[3:0] = C[27:24]; c32[3:0] = C[31:28]; COUT = C_out;
  //   flag_c = CSR_FLAG[4]; flag_c_b = CSR_FLAG[5]; flag_gt = CSR_FLAG[10]; flag_GT_unsign = CSR_FLAG[14];
  //   flag_gte = CSR_FLAG[11]; flag_lt = CSR_FLAG[8]; flag_lte = CSR_FLAG[9]; flag_LTE_unsign = CSR_FLAG[13];
  //   flag_n = CSR_FLAG[2]; flag_n_b = CSR_FLAG[3]; flag_v = CSR_FLAG[6]; flag_v_b = CSR_FLAG[7];
  //   flag_z = CSR_FLAG[0]; flag_z_b = CSR_FLAG[1]; nflag_a_is_zero = flagIsNotZ; OUT4[3:0] = OUT[3:0];
  //   out4_t = OUT[4]; OUT8[3:0] = OUT[7:4]; out8_t = OUT[8]; OUT12[3:0] = OUT[11:8]; out12_t = OUT[12];
  //   OUT16[3:0] = OUT[15:12]; out16_t = OUT[16]; OUT20[3:0] = OUT[19:16]; out20_t = OUT[20]; OUT24[3:0] = OUT[23:20];
  //   out24_t = OUT[24]; OUT28[3:0] = OUT[27:24]; out28_t = OUT[28]; OUT32[3:0] = OUT[31:28]; N_out = OUT[31]

  // Notes on the sheet:
  //   alu_ctrl: default 31
  //   Overflow Logic
  //   Zero Flag
endmodule
