// Digital circuit ir.dig as structural Verilog
module ir (
  input  [31:0] DATA_IN,
  input  LOAD,
  input  CLK,
  input  [3:0] ir_sel,
  input  [31:0] RegB,
  output [7:0] OPCODE,
  output [7:0] ADDR_A,
  output [7:0] ADDR_B,
  output [7:0] ADDR_W,
  output [23:0] ADDR_ABS,
  output [23:0] OFFSET,
  output [2:0] COND,
  output MUX1_SEL,
  output MUX2_SEL,
  output [31:0] ir_imm_out
);

  Register #(.Bits(32)) register_1 (.D(DATA_IN), .C(CLK), .en(LOAD));  // open: Q
  Multiplexer #(.Selector_Bits(4), .Bits(32)) multiplexer_1 (
    .sel(ir_sel), .in_0(RegB), .in_1({{24{1'b0}}, DATA_IN[7:0]}), .in_2({{25{DATA_IN[7]}}, DATA_IN[6:0]}),
    .in_3({{21{DATA_IN[23]}}, DATA_IN[22:12]}), .in_4({{20{1'b0}}, DATA_IN[11:0]}),
    .in_5({{27{1'b0}}, DATA_IN[12:8]}), .in_6({{27{1'b0}}, DATA_IN[20:16]}),
    .in_7({{16{1'b0}}, DATA_IN[15:0]}), .in_8({{17{DATA_IN[15]}}, DATA_IN[14:0]}),
    .in_9({{9{DATA_IN[23]}}, DATA_IN[22:0]}), .in_10({DATA_IN[23:8], {16{1'b0}}}),
    .in_11({DATA_IN[23:4], {12{1'b0}}}), .in_12({{15{DATA_IN[15]}}, DATA_IN[14:0], 2'b00}),
    .in_13({{7{DATA_IN[23]}}, DATA_IN[22:0], 2'b00}), .in_14({32{1'b0}}), .in_15({32{1'b0}}), .out(ir_imm_out));

  assign ADDR_A = DATA_IN[23:16];
  assign ADDR_ABS = DATA_IN[23:0];
  assign ADDR_B = DATA_IN[15:8];
  assign ADDR_W = DATA_IN[7:0];
  assign COND = DATA_IN[2:0];
  assign MUX1_SEL = DATA_IN[0];
  assign MUX2_SEL = DATA_IN[1];
  assign OFFSET = DATA_IN[23:0];
  assign OPCODE = DATA_IN[31:24];

  // Other names for the same wires on the sheet: imm_out[31:0] = ir_imm_out; ir1[7:0] = DATA_IN[7:0];
  //   ir2[31:0] = {{25{DATA_IN[7]}}, DATA_IN[6:0]}; ir4[11:0] = DATA_IN[11:0]; ir7[15:0] = DATA_IN[15:0];
  //   ir8[31:0] = {{17{DATA_IN[15]}}, DATA_IN[14:0]}; ir9[31:0] = {{9{DATA_IN[23]}}, DATA_IN[22:0]};
  //   ir12[31:2] = {{15{DATA_IN[15]}}, DATA_IN[14:0]}; ir13[31:2] = {{7{DATA_IN[23]}}, DATA_IN[22:0]};
  //   ir_bus[23:0] = DATA_IN[23:0]; ir_bus_main[31:0] = DATA_IN; ir11[31:12] = DATA_IN[23:4];
  //   ir7__gt_24[23:0] = {24{DATA_IN[7]}}; ir5[4:0] = DATA_IN[12:8]; ir10[31:16] = DATA_IN[23:8];
  //   ir3[31:0] = {{21{DATA_IN[23]}}, DATA_IN[22:12]}; ir15__gt_14[13:0] = {14{DATA_IN[15]}};
  //   ir15__gt_16[15:0] = {16{DATA_IN[15]}}; ir6[4:0] = DATA_IN[20:16]; ir23__gt_6[5:0] = {6{DATA_IN[23]}};
  //   ir23__gt_8[7:0] = {8{DATA_IN[23]}}; ir23__gt_20[19:0] = {20{DATA_IN[23]}}; reg_b[31:0] = RegB

  // Notes on the sheet:
  //   DATA_IN: default 3735928559
  //   RegB: default 2882356583
endmodule

/* Test case ir tests:
CLK LOAD DATA_IN IR_BUS OPCODE ADDR_A ADDR_B ADDR_W ADDR_ABS OFFSET COND MUX1_SEL MUX2_SEL

# A — LOAD=0 never captures
C 1 0x00000000 0x00000000 0x00 0x00 0x00 0x00 0x000000 0x000000 0 0 0
0 0 0xDEADBEEF 0x00000000 0x00 0x00 0x00 0x00 0x000000 0x000000 0 0 0
C 0 0xDEADBEEF 0x00000000 0x00 0x00 0x00 0x00 0x000000 0x000000 0 0 0
C 1 0x01020304 0x01020304 0x01 0x02 0x03 0x04 0x020304 0x020304 4 0 0

# B — slice spot-check words
# zeros
C 1 0x00000000 0x00000000 0x00 0x00 0x00 0x00 0x000000 0x000000 0 0 0
0 1 0x00000000 0x00000000 0x00 0x00 0x00 0x00 0x000000 0x000000 0 0 0
# distinct bytes
C 1 0x01020304 0x01020304 0x01 0x02 0x03 0x04 0x020304 0x020304 4 0 0
0 1 0x01020304 0x01020304 0x01 0x02 0x03 0x04 0x020304 0x020304 4 0 0
# all ones
C 1 0xFFFFFFFF 0xFFFFFFFF 0xFF 0xFF 0xFF 0xFF 0xFFFFFF 0xFFFFFF 7 1 1
0 1 0xFFFFFFFF 0xFFFFFFFF 0xFF 0xFF 0xFF 0xFF 0xFFFFFF 0xFFFFFF 7 1 1
# pattern
C 1 0xCAFEBABE 0xCAFEBABE 0xCA 0xFE 0xBA 0xBE 0xFEBABE 0xFEBABE 6 0 1
0 1 0xCAFEBABE 0xCAFEBABE 0xCA 0xFE 0xBA 0xBE 0xFEBABE 0xFEBABE 6 0 1
# low byte 07
C 1 0x00000007 0x00000007 0x00 0x00 0x00 0x07 0x000007 0x000007 7 1 1
0 1 0x00000007 0x00000007 0x00 0x00 0x00 0x07 0x000007 0x000007 7 1 1
# opcode byte 0x00
C 1 0x00010203 0x00010203 0x00 0x01 0x02 0x03 0x010203 0x010203 3 1 1
0 1 0x00010203 0x00010203 0x00 0x01 0x02 0x03 0x010203 0x010203 3 1 1
# opcode byte 0x01
C 1 0x01010203 0x01010203 0x01 0x01 0x02 0x03 0x010203 0x010203 3 1 1
0 1 0x01010203 0x01010203 0x01 0x01 0x02 0x03 0x010203 0x010203 3 1 1
# opcode byte 0x02
C 1 0x02010203 0x02010203 0x02 0x01 0x02 0x03 0x010203 0x010203 3 1 1
0 1 0x02010203 0x02010203 0x02 0x01 0x02 0x03 0x010203 0x010203 3 1 1
# opcode byte 0x03
C 1 0x03010203 0x03010203 0x03 0x01 0x02 0x03 0x010203 0x010203 3 1 1
0 1 0x03010203 0x03010203 0x03 0x01 0x02 0x03 0x010203 0x010203 3 1 1
# opcode byte 0x04
C 1 0x04010203 0x04010203 0x04 0x01 0x02 0x03 0x010203 0x010203 3 1 1
0 1 0x04010203 0x04010203 0x04 0x01 0x02 0x03 0x010203 0x010203 3 1 1
# opcode byte 0x05
C 1 0x05010203 0x05010203 0x05 0x01 0x02 0x03 0x010203 0x010203 3 1 1
0 1 0x05010203 0x05010203 0x05 0x01 0x02 0x03 0x010203 0x010203 3 1 1
# opcode byte 0x06
C 1 0x06010203 0x06010203 0x06 0x01 0x02 0x03 0x010203 0x010203 3 1 1
0 1 0x06010203 0x06010203 0x06 0x01 0x02 0x03 0x010203 0x010203 3 1 1
# opcode byte 0x07
C 1 0x07010203 0x07010203 0x07 0x01 0x02 0x03 0x010203 0x010203 3 1 1
0 1 0x07010203 0x07010203 0x07 0x01 0x02 0x03 0x010203 0x010203 3 1 1
# opcode byte 0x08
C 1 0x08010203 0x08010203 0x08 0x01 0x02 0x03 0x010203 0x010203 3 1 1
0 1 0x08010203 0x08010203 0x08 0x01 0x02 0x03 0x010203 0x010203 3 1 1
# opcode byte 0x09
C 1 0x09010203 0x09010203 0x09 0x01 0x02 0x03 0x010203 0x010203 3 1 1
0 1 0x09010203 0x09010203 0x09 0x01 0x02 0x03 0x010203 0x010203 3 1 1
# opcode byte 0x0A
C 1 0x0A010203 0x0A010203 0x0A 0x01 0x02 0x03 0x010203 0x010203 3 1 1
0 1 0x0A010203 0x0A010203 0x0A 0x01 0x02 0x03 0x010203 0x010203 3 1 1
# opcode byte 0x0B
C 1 0x0B010203 0x0B010203 0x0B 0x01 0x02 0x03 0x010203 0x010203 3 1 1
0 1 0x0B010203 0x0B010203 0x0B 0x01 0x02 0x03 0x010203 0x010203 3 1 1
# opcode byte 0x0C
C 1 0x0C010203 0x0C010203 0x0C 0x01 0x02 0x03 0x010203 0x010203 3 1 1
0 1 0x0C010203 0x0C010203 0x0C 0x01 0x02 0x03 0x010203 0x010203 3 1 1
# opcode byte 0x0D
C 1 0x0D010203 0x0D010203 0x0D 0x01 0x02 0x03 0x010203 0x010203 3 1 1
0 1 0x0D010203 0x0D010203 0x0D 0x01 0x02 0x03 0x010203 0x010203 3 1 1
# opcode byte 0x0E
C 1 0x0E010203 0x0E010203 0x0E 0x01 0x02 0x03 0x010203 0x010203 3 1 1
0 1 0x0E010203 0x0E010203 0x0E 0x01 0x02 0x03 0x010203 0x010203 3 1 1
# opcode byte 0x0F
C 1 0x0F010203 0x0F010203 0x0F 0x01 0x02 0x03 0x010203 0x010203 3 1 1
0 1 0x0F010203 0x0F010203 0x0F 0x01 0x02 0x03 0x010203 0x010203 3 1 1
# opcode byte 0x10
C 1 0x10010203 0x10010203 0x10 0x01 0x02 0x03 0x010203 0x010203 3 1 1
0 1 0x10010203 0x10010203 0x10 0x01 0x02 0x03 0x010203 0x010203 3 1 1
# opcode byte 0x11
C 1 0x11010203 0x11010203 0x11 0x01 0x02 0x03 0x010203 0x010203 3 1 1
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*/
