// Digital circuit mul-div.dig as structural Verilog
module mul_div (
  input  [31:0] A,
  input  [31:0] B,
  output [31:0] mul_out
);

  wire [63:32] mul_1_mul;

  Mul #(.Bits(32)) mul_1 (.a(A), .b(B), .mul({mul_1_mul, mul_out}));

  // Notes on the sheet:
  //   A: default 51
  //   B: default 2
endmodule
